# Fritzing sketch ArduTrackv1.2 (saved by Fritzing 0.8.3b)

parts:
  Arduino1 = Arduino  # not connected
  Part1 = Arduino GSM Shield
  GPS1 = Adafruit Ultimate GPS Breakout

nets:
  N1: Part1.PWM_D9, GPS1.RX
  N2: Part1.D8, GPS1.TX
  5V: Part1.5V, GPS1.VIN
  N3: Part1.AGND, GPS1.GND

custom parts:
  Arduino: The awesome Arduino microcontroller
