# Fritzing sketch Cat Tracker (saved by Fritzing 0.8.3b)
circuit board: 16.9333cm x 5.64444cm

parts:
  Part1 = LilyPad Power Supply
  U1 = XBEE-1 [package=xbee-1_lock]  # not connected
  Part2 = LilyPad Arduino USB  # not connected
  GPS1 = Adafruit Ultimate GPS Breakout
  Part3 = LilyPad XBee

nets:
  N1: Part1.+, Part3.VCC
  GND: Part1.GND, GPS1.GND, Part3.GND
  3.3V: GPS1.3.3V, Part3.3.3V
